# Fritzing sketch Connection - CC2530 (saved by Fritzing 0.8.7b)
breadboards: 1

parts:
  Parte1 = Arduino Uno (Rev3)
  J1 = female pin header, 11 pins [form="♀ (female)"]
  J4 = female pin header, 11 pins [form="♀ (female)"]  # not connected
  LLC_5V_3V1 = Logic Level Converter 5V - 3.3V [chip_label=LLC_5V_3V package="DIP (Dual Inline) [THT]"]
  J2 = female pin header, 1 pin [form="♀ (female)"]
  J5 = female pin header, 1 pin [form="♀ (female)"]
  J3 = female pin header, 1 pin [form="♀ (female)"]

nets:
  N1: Parte1.D2, LLC_5V_3V1.HV_CH1
  N2: Parte1.D3_PWM, LLC_5V_3V1.HV_CH2
  N3: Parte1.D4, LLC_5V_3V1.HV_CH3
  N4: Parte1.3V3, LLC_5V_3V1.VCC_3V
  N5: Parte1.5V, J1.pin10
  N6: Parte1.GND, J1.pin1, LLC_5V_3V1.GND_5V, LLC_5V_3V1.GND_3V
  N7: J1.pin3, LLC_5V_3V1.LV_CH3, J2.pin1
  N8: J1.pin4, LLC_5V_3V1.LV_CH2, J5.pin1
  N9: J1.pin6, LLC_5V_3V1.LV_CH1, J3.pin1

notes:
  VSS
  VCC
  RSV
  PWM
  RESET
  P2.2
  P2.1
  Outsize female pin header refer
  to XBee Adapter Board
  Inside female pin header refer
  to CC2530 board

custom parts:
  Logic Level Converter 5V - 3.3V: A logic level converter to adapt 5V system to 3.3V system.
