# Fritzing sketch Connection - PIC18F2xxx PIC18F4xxx (saved by Fritzing 0.8.3b)
breadboards: 1

parts:
  Parte1 = Arduino Uno (Rev3)
  IC1 = PICAXE-40X2-3V [package=THT]
  R1 = Resistor [tolerance=±5% resistance=220 package=THT]
  R2 = Resistor [tolerance=±5% resistance=220 package=THT]
  R3 = Resistor [tolerance=±5% resistance=220 package=THT]
  R4 = Resistor [tolerance=±5% resistance=220 package=THT]

nets:
  N1: Parte1.GND, IC1.0V
  N2: Parte1.D2, R1.Pin_0
  N3: Parte1.D5_PWM, R4.Pin_0
  N4: Parte1.D6_PWM, R3.Pin_0
  N5: Parte1.D7, R2.Pin_0
  N6: Parte1.5V, IC1.+3V6
  N7: IC1.Reset, R1.Pin_1
  N8: IC1.B.5, R4.Pin_1
  N9: IC1.B.6, R3.Pin_1
  N10: IC1.B.7, R2.Pin_1
